// Logisim project Lab4.circ as structural Verilog: 1 circuit, main circuit main
module main (
  input  in_1,
  input  in_2,
  input  in_3,
  input  in_4
);

  wire and_1_out, and_2_out, and_3_out, and_4_out, or_1_out;

  and and_1 (and_1_out, ~in_1, in_2, ~in_3, in_4);  // AND_Gate
  and and_2 (and_2_out, in_1, ~in_2, in_3, ~in_4);  // AND_Gate
  and and_3 (and_3_out, in_1, in_2, in_3, in_4);
  and and_4 (and_4_out, ~in_1, ~in_2, ~in_3, ~in_4);  // AND_Gate
  or or_1 (or_1_out, and_1_out, and_2_out, and_3_out, and_4_out);
  // Probe on or_1_out
endmodule
