// Logisim project LAB-5.circ as structural Verilog: 1 circuit, main circuit main
module main (
  input  A1,
  input  A0,
  input  B1,
  input  B0
);

  wire and_1_out, and_2_out, and_3_out, and_4_out, and_5_out, and_6_out, and_7_out, and_8_out, and_9_out,
       and_10_out, and_11_out, or_1_out, or_2_out, or_3_out, or_4_out;

  and and_1 (and_1_out, A1, ~B1);  // AND_Gate
  and and_2 (and_2_out, A1, B1);
  and and_3 (and_3_out, ~A1, ~B1);  // AND_Gate
  and and_4 (and_4_out, ~A1, B1);  // AND_Gate
  and and_5 (and_5_out, A0, ~B0);  // AND_Gate
  and and_6 (and_6_out, A0, B0);
  and and_7 (and_7_out, ~A0, ~B0);  // AND_Gate
  and and_8 (and_8_out, ~A0, B0);  // AND_Gate
  or or_1 (or_1_out, and_2_out, and_3_out);
  or or_2 (or_2_out, and_6_out, and_7_out);
  and and_9 (and_9_out, or_1_out, and_5_out);
  and and_10 (and_10_out, or_1_out, and_8_out);
  // Probe on or_3_out
  or or_3 (or_3_out, and_1_out, and_9_out);
  and and_11 (and_11_out, or_1_out, or_2_out);
  // Probe on and_11_out
  or or_4 (or_4_out, and_4_out, and_10_out);
  // Probe on or_4_out

  // Notes on the sheet:
  //   G
  //   E
  //   L
endmodule
